# Fritzing sketch spacegun (saved by Fritzing 0.9.3b)
circuit board: 8.46667cm x 5.64444cm
breadboards: 1

parts:
  Space_Gun = Arduino Uno (Rev3)
  R1 = Resistor [tolerance=±5% resistance=220 package=THT]
  R2 = Resistor [tolerance=±5% resistance=220 package=THT]
  R3 = Resistor [tolerance=±5% resistance=220 package=THT]
  LED1 = RGB LED (com. cathode, rgb) [package="5 mm [THT]"]
  S1 = Pushbutton [package=THT]

nets:
  N1: Space_Gun.D10_PWM/SS, R3.Pin_0
  N2: Space_Gun.D11_PWM/MOSI, R2.Pin_0
  N3: Space_Gun.D12/MISO, R1.Pin_0
  N4: Space_Gun.GND, LED1.common_cathode, S1.leg0
  N5: Space_Gun.D4, S1.leg1
  N6: R1.Pin_1, LED1.blue_anode
  N7: R2.Pin_1, LED1.green_anode
  N8: R3.Pin_1, LED1.red_anode

// code stored in the sketch: spacegun.ino

const int RED_PIN = 10;
const int GREEN_PIN = 11;
const int BLUE_PIN = 12;

int red = 0;
int green = 0;
int blue = 0;

void setup() {
	pinMode(RED_PIN, OUTPUT);
  pinMode(GREEN_PIN, OUTPUT);
	pinMode(BLUE_PIN, OUTPUT);

	red = random(0, 256);
	green = random(0, 256);
	blue = random(0, 256);
}

int jitter(int value) {
	return abs((value + random(-50, 50)) % 256);
}

void loop() {

	red = jitter(red);
	green = jitter(green);
	blue = jitter(blue);

	analogWrite(RED_PIN, red);
	analogWrite(GREEN_PIN, green);
	analogWrite(BLUE_PIN, blue);

	delay(10);
}
